# Fritzing sketch sketch1 (saved by Fritzing 1.0.2b)
breadboards: 1

parts:
  Componente1 = Arduino Uno (Rev3)
  Componente2 = Arduino GSM Shield
  BAT1 = Battery Holders [package=battery-aaa]
  M1 = fc-51 [package=THT]  # not connected
  LED1 = LED - 3mm [color="Red (633nm)" current=0.030A package="3 mm [THT]"]
  J1 = Piezo Speaker
  M2 = fc-51 [package=THT]

nets:
  N1: Componente1.D8, Componente2.D8
  N2: Componente1.D9_PWM, M2.pin1
  N3: Componente1.D10_PWM/SS, Componente2.SS/PWM_D10
  N4: Componente1.D6_PWM, LED1.cathode, J1.pin1
  N5: Componente1.5V, M2.pin3
  N6: Componente1.GND, J1.pin2, M2.pin2
  N7: Componente2.AGND, BAT1.-
  N8: Componente2.VIN, BAT1.+
